// Logisim project vpu.circ as structural Verilog: 12 circuits, main circuit VPU
module VPU (
  input  in_1,
  input  in_2,
  input  [5:0] in_3,
  input  [4:0] in_4,
  input  [4:0] in_5,
  input  [31:0] in_6,
  input  [31:0] in_7,
  input  [23:0] in_8,
  output [31:0] VRegOutHi,
  output [31:0] VRegOutLo,
  output VPUError,
  output VBus32,
  output VBus64
);

  wire alu_a_sel, Config, isSV, load_imm, sign_ext_imm, WEn;
  wire [1:0] Reg_In_Sel;
  wire [2:0] ALU_Op;
  wire [4:0] len, num16;
  wire [15:0] alu_out0, alu_out1, alu_out2, alu_out3, imm0, imm1, imm2, imm3, multiplexer_1_out,
       multiplexer_2_out, multiplexer_3_out, multiplexer_4_out, ram0, ram1, ram2, ram3, regfile_1_read1_15_0,
       regfile_1_read1_31_16, regfile_1_read1_47_32, regfile_1_read1_63_48, regfile_1_read2_15_0,
       regfile_1_read2_31_16, regfile_1_read2_47_32, regfile_1_read2_63_48;

  LV_RAM_Decoder lv_ram_decoder_1 (
    .vrd(in_4), .num16(num16), .length(len), .RAMOutHi(in_6), .RAMOutLo(in_7), .Read1_63_48(ram3),
    .Read1_47_32(ram2), .Read1_31_16(ram1), .Read1_15_0(ram0));
  Multiplexer #(.select(2), .width(16), .enable("false")) multiplexer_1 (
    .in0(alu_out3), .in1(ram3), .in2(in_8[15:0]), .in3(imm3), .out(multiplexer_1_out), .sel(Reg_In_Sel));
  // Probe on Reg_In_Sel
  Multiplexer #(.select(2), .width(16), .enable("false")) multiplexer_2 (
    .in0(alu_out2), .in1(ram2), .in2(in_8[15:0]), .in3(imm2), .out(multiplexer_2_out), .sel(Reg_In_Sel));
  Multiplexer #(.select(2), .width(16), .enable("false")) multiplexer_3 (
    .in0(alu_out1), .in1(ram1), .in2(in_8[15:0]), .in3(imm1), .out(multiplexer_3_out), .sel(Reg_In_Sel));
  Multiplexer #(.select(2), .width(16), .enable("false")) multiplexer_4 (
    .in0(alu_out0), .in1(ram0), .in2(in_8[15:0]), .in3(imm0), .out(multiplexer_4_out), .sel(Reg_In_Sel));
  RegFile regfile_1 (
    .Reconfig(Config), .CLK(in_2), .Write_EN(WEn), .vrd(in_4), .vrs(in_5), .Write_63_48(multiplexer_1_out),
    .Write_47_32(multiplexer_2_out), .Write_31_16(multiplexer_3_out), .Write_15_0(multiplexer_4_out),
    .Read2_63_48(regfile_1_read2_63_48), .Read2_47_32(regfile_1_read2_47_32),
    .Read2_31_16(regfile_1_read2_31_16), .Read2_15_0(regfile_1_read2_15_0),
    .Read1_63_48(regfile_1_read1_63_48), .Read1_47_32(regfile_1_read1_47_32),
    .Read1_31_16(regfile_1_read1_31_16), .Read1_15_0(regfile_1_read1_15_0), .num16(num16), .length(len));
  ALU_A alu_a_1 (
    .load_imm(load_imm), .reg3(regfile_1_read1_63_48), .reg2(regfile_1_read1_47_32),
    .reg1(regfile_1_read1_31_16), .reg0(regfile_1_read1_15_0), .vrs(in_5), .sign_ext_imm(sign_ext_imm),
    .ALUa3(imm3), .ALUa2(imm2), .ALUa1(imm1), .ALUa0(imm0), .B3(regfile_1_read2_63_48),
    .B2(regfile_1_read2_47_32), .B1(regfile_1_read2_31_16), .B0(regfile_1_read2_15_0), .alu_a_sel(alu_a_sel));
  SV_Reg sv_reg_1 (
    .vrd(in_4), .num16(num16), .length(len), .EX(in_1), .isSV(isSV), .in3(regfile_1_read1_63_48),
    .in2(regfile_1_read1_47_32), .in1(regfile_1_read1_31_16), .in0(regfile_1_read1_15_0), .VBus32(VBus32),
    .VBus64(VBus64), .VRegOutHi(VRegOutHi), .VRegOutLo(VRegOutLo));
  _64bALU u_64balu_1 (
    .A0(imm3), .A1(imm2), .A2(imm1), .A3(imm0), .B0(regfile_1_read2_63_48), .B1(regfile_1_read2_47_32),
    .B2(regfile_1_read2_31_16), .B3(regfile_1_read2_15_0), .ALU_Op(ALU_Op), .Q0(alu_out3), .Q1(alu_out2),
    .Q2(alu_out1), .Q3(alu_out0));
  Control control_1 (
    .Opcode(in_3), .Reg_In(Reg_In_Sel), .Write_En(WEn), .is_SV(isSV), .load_imm(load_imm),
    .sign_ext_imm(sign_ext_imm), .ALU_Op(ALU_Op), .EX(in_1), .Config(Config), .alu_a_sel(alu_a_sel));

  assign VPUError = 1'b0;

  // Other names for the same wires on the sheet: CLK = in_2; EX = in_1; RAMOutHi[31:0] = in_6; RAMOutLo[31:0] = in_7;
  //   RegOut2[23:0] = in_8; regout2_t[15:0] = in_8[15:0]; vop[5:0] = in_3; vrd[4:0] = in_4; vrs[4:0] = in_5
endmodule

module RegFile (
  input  Reconfig,
  input  CLK,
  input  Write_EN,
  input  [4:0] vrd,
  input  [4:0] vrs,
  input  [15:0] Write_63_48,
  input  [15:0] Write_47_32,
  input  [15:0] Write_31_16,
  input  [15:0] Write_15_0,
  output [15:0] Read2_63_48,
  output [15:0] Read2_47_32,
  output [15:0] Read2_31_16,
  output [15:0] Read2_15_0,
  output [15:0] Read1_63_48,
  output [15:0] Read1_47_32,
  output [15:0] Read1_31_16,
  output [15:0] Read1_15_0,
  output [4:0] num16,
  output [4:0] length
);

  wire _0, _1, _2, _3, _4, _5, _6, _7, _8, _9, _10, _11, _12, _13, _14, _15, _16, _17, _18, _19, _20, _21,
       _22, _23, _24, _25, _26, _27, _28, _29, _30, _31, _32, _33, _34, _35, _36, _37, _38, _39, _40, _41,
       _42, _43, _44, _45, _46, _47, _48, _49, _50, _51, _52, _53, _54, _55, _56, _57, _58, _59, _60, _61,
       _62, _63, en0, en1, en2, en3, en4, en5, en6, en7, en8, en9, en10, en11, en12, en13, en14, en15, en16,
       en17, en18, en19, en20, en21, en22, en23, en24, en25, en26, en27, en28, en29, en30, en31;
  wire [15:0] R0, R1, R2, R3, R4, R5, R6, R7;

  Register_part #(.width(5)) num_16_regs (.D(vrd), .en(Reconfig), .Q(num16), .clk(CLK));  // open: clr
  Register_part #(.width(5)) vector_len (.D(vrs), .en(Reconfig), .Q(length), .clk(CLK));  // open: clr
  Demultiplexer #(.select(5), .enable("false")) demultiplexer_1 (
    .out0(en0), .out1(en1), .out2(en2), .out3(en3), .out4(en4), .out5(en5), .out6(en6), .out7(en7),
    .out8(en8), .out9(en9), .out10(en10), .out11(en11), .out12(en12), .out13(en13), .out14(en14),
    .out15(en15), .out16(en16), .out17(en17), .out18(en18), .out19(en19), .out20(en20), .out21(en21),
    .out22(en22), .out23(en23), .out24(en24), .out25(en25), .out26(en26), .out27(en27), .out28(en28),
    .out29(en29), .out30(en30), .out31(en31), .in(Write_EN), .sel(vrd));
  Register register_1 (
    .Out_63_48(R3), .Out_47_32(R2), .Out_31_16(R1), .Out_15_0(R0), .CLK(CLK), .In_63_48(Write_63_48),
    .In_47_32(Write_47_32), .In_31_16(Write_31_16), .In_15_0(Write_15_0), .Write_En(en0), .Bus_En(_0),
    .Bus_En2(_32), .Out2_63_48(R7), .Out2_47_32(R6), .Out2_31_16(R5), .Out2_15_0(R4));
  Register register_2 (
    .Out_63_48(R3), .Out_47_32(R2), .Out_31_16(R1), .Out_15_0(R0), .CLK(CLK), .In_63_48(Write_63_48),
    .In_47_32(Write_47_32), .In_31_16(Write_31_16), .In_15_0(Write_15_0), .Write_En(en1), .Bus_En(_1),
    .Bus_En2(_33), .Out2_63_48(R7), .Out2_47_32(R6), .Out2_31_16(R5), .Out2_15_0(R4));
  Register register_3 (
    .Out_63_48(R3), .Out_47_32(R2), .Out_31_16(R1), .Out_15_0(R0), .CLK(CLK), .In_63_48(Write_63_48),
    .In_47_32(Write_47_32), .In_31_16(Write_31_16), .In_15_0(Write_15_0), .Write_En(en2), .Bus_En(_2),
    .Bus_En2(_34), .Out2_63_48(R7), .Out2_47_32(R6), .Out2_31_16(R5), .Out2_15_0(R4));
  Register register_4 (
    .Out_63_48(R3), .Out_47_32(R2), .Out_31_16(R1), .Out_15_0(R0), .CLK(CLK), .In_63_48(Write_63_48),
    .In_47_32(Write_47_32), .In_31_16(Write_31_16), .In_15_0(Write_15_0), .Write_En(en3), .Bus_En(_3),
    .Bus_En2(_35), .Out2_63_48(R7), .Out2_47_32(R6), .Out2_31_16(R5), .Out2_15_0(R4));
  Register register_5 (
    .Out_63_48(R3), .Out_47_32(R2), .Out_31_16(R1), .Out_15_0(R0), .CLK(CLK), .In_63_48(Write_63_48),
    .In_47_32(Write_47_32), .In_31_16(Write_31_16), .In_15_0(Write_15_0), .Write_En(en4), .Bus_En(_4),
    .Bus_En2(_36), .Out2_63_48(R7), .Out2_47_32(R6), .Out2_31_16(R5), .Out2_15_0(R4));
  Register register_6 (
    .Out_63_48(R3), .Out_47_32(R2), .Out_31_16(R1), .Out_15_0(R0), .CLK(CLK), .In_63_48(Write_63_48),
    .In_47_32(Write_47_32), .In_31_16(Write_31_16), .In_15_0(Write_15_0), .Write_En(en5), .Bus_En(_5),
    .Bus_En2(_37), .Out2_63_48(R7), .Out2_47_32(R6), .Out2_31_16(R5), .Out2_15_0(R4));
  Register register_7 (
    .Out_63_48(R3), .Out_47_32(R2), .Out_31_16(R1), .Out_15_0(R0), .CLK(CLK), .In_63_48(Write_63_48),
    .In_47_32(Write_47_32), .In_31_16(Write_31_16), .In_15_0(Write_15_0), .Write_En(en6), .Bus_En(_6),
    .Bus_En2(_38), .Out2_63_48(R7), .Out2_47_32(R6), .Out2_31_16(R5), .Out2_15_0(R4));
  Register register_8 (
    .Out_63_48(R3), .Out_47_32(R2), .Out_31_16(R1), .Out_15_0(R0), .CLK(CLK), .In_63_48(Write_63_48),
    .In_47_32(Write_47_32), .In_31_16(Write_31_16), .In_15_0(Write_15_0), .Write_En(en7), .Bus_En(_7),
    .Bus_En2(_39), .Out2_63_48(R7), .Out2_47_32(R6), .Out2_31_16(R5), .Out2_15_0(R4));
  Register register_9 (
    .Out_63_48(R3), .Out_47_32(R2), .Out_31_16(R1), .Out_15_0(R0), .CLK(CLK), .In_63_48(Write_63_48),
    .In_47_32(Write_47_32), .In_31_16(Write_31_16), .In_15_0(Write_15_0), .Write_En(en8), .Bus_En(_8),
    .Bus_En2(_40), .Out2_63_48(R7), .Out2_47_32(R6), .Out2_31_16(R5), .Out2_15_0(R4));
  Register register_10 (
    .Out_63_48(R3), .Out_47_32(R2), .Out_31_16(R1), .Out_15_0(R0), .CLK(CLK), .In_63_48(Write_63_48),
    .In_47_32(Write_47_32), .In_31_16(Write_31_16), .In_15_0(Write_15_0), .Write_En(en9), .Bus_En(_9),
    .Bus_En2(_41), .Out2_63_48(R7), .Out2_47_32(R6), .Out2_31_16(R5), .Out2_15_0(R4));
  Register register_11 (
    .Out_63_48(R3), .Out_47_32(R2), .Out_31_16(R1), .Out_15_0(R0), .CLK(CLK), .In_63_48(Write_63_48),
    .In_47_32(Write_47_32), .In_31_16(Write_31_16), .In_15_0(Write_15_0), .Write_En(en10), .Bus_En(_10),
    .Bus_En2(_42), .Out2_63_48(R7), .Out2_47_32(R6), .Out2_31_16(R5), .Out2_15_0(R4));
  Register register_12 (
    .Out_63_48(R3), .Out_47_32(R2), .Out_31_16(R1), .Out_15_0(R0), .CLK(CLK), .In_63_48(Write_63_48),
    .In_47_32(Write_47_32), .In_31_16(Write_31_16), .In_15_0(Write_15_0), .Write_En(en11), .Bus_En(_11),
    .Bus_En2(_43), .Out2_63_48(R7), .Out2_47_32(R6), .Out2_31_16(R5), .Out2_15_0(R4));
  Register register_13 (
    .Out_63_48(R3), .Out_47_32(R2), .Out_31_16(R1), .Out_15_0(R0), .CLK(CLK), .In_63_48(Write_63_48),
    .In_47_32(Write_47_32), .In_31_16(Write_31_16), .In_15_0(Write_15_0), .Write_En(en12), .Bus_En(_12),
    .Bus_En2(_44), .Out2_63_48(R7), .Out2_47_32(R6), .Out2_31_16(R5), .Out2_15_0(R4));
  Register register_14 (
    .Out_63_48(R3), .Out_47_32(R2), .Out_31_16(R1), .Out_15_0(R0), .CLK(CLK), .In_63_48(Write_63_48),
    .In_47_32(Write_47_32), .In_31_16(Write_31_16), .In_15_0(Write_15_0), .Write_En(en13), .Bus_En(_13),
    .Bus_En2(_45), .Out2_63_48(R7), .Out2_47_32(R6), .Out2_31_16(R5), .Out2_15_0(R4));
  Register register_15 (
    .Out_63_48(R3), .Out_47_32(R2), .Out_31_16(R1), .Out_15_0(R0), .CLK(CLK), .In_63_48(Write_63_48),
    .In_47_32(Write_47_32), .In_31_16(Write_31_16), .In_15_0(Write_15_0), .Write_En(en14), .Bus_En(_14),
    .Bus_En2(_46), .Out2_63_48(R7), .Out2_47_32(R6), .Out2_31_16(R5), .Out2_15_0(R4));
  Register register_16 (
    .Out_63_48(R3), .Out_47_32(R2), .Out_31_16(R1), .Out_15_0(R0), .CLK(CLK), .In_63_48(Write_63_48),
    .In_47_32(Write_47_32), .In_31_16(Write_31_16), .In_15_0(Write_15_0), .Write_En(en15), .Bus_En(_15),
    .Bus_En2(_47), .Out2_63_48(R7), .Out2_47_32(R6), .Out2_31_16(R5), .Out2_15_0(R4));
  Decoder #(.select(5), .enable("false")) decoder_1 (
    .out0(_0), .out1(_1), .out2(_2), .out3(_3), .out4(_4), .out5(_5), .out6(_6), .out7(_7), .out8(_8),
    .out9(_9), .out10(_10), .out11(_11), .out12(_12), .out13(_13), .out14(_14), .out15(_15), .out16(_16),
    .out17(_17), .out18(_18), .out19(_19), .out20(_20), .out21(_21), .out22(_22), .out23(_23), .out24(_24),
    .out25(_25), .out26(_26), .out27(_27), .out28(_28), .out29(_29), .out30(_30), .out31(_31), .sel(vrd));
  Decoder #(.select(5), .enable("false")) decoder_2 (
    .out0(_32), .out1(_33), .out2(_34), .out3(_35), .out4(_36), .out5(_37), .out6(_38), .out7(_39),
    .out8(_40), .out9(_41), .out10(_42), .out11(_43), .out12(_44), .out13(_45), .out14(_46), .out15(_47),
    .out16(_48), .out17(_49), .out18(_50), .out19(_51), .out20(_52), .out21(_53), .out22(_54), .out23(_55),
    .out24(_56), .out25(_57), .out26(_58), .out27(_59), .out28(_60), .out29(_61), .out30(_62), .out31(_63),
    .sel(vrs));
  Register register_17 (
    .Out_63_48(R3), .Out_47_32(R2), .Out_31_16(R1), .Out_15_0(R0), .CLK(CLK), .In_63_48(Write_63_48),
    .In_47_32(Write_47_32), .In_31_16(Write_31_16), .In_15_0(Write_15_0), .Write_En(en16), .Bus_En(_16),
    .Bus_En2(_48), .Out2_63_48(R7), .Out2_47_32(R6), .Out2_31_16(R5), .Out2_15_0(R4));
  Register register_18 (
    .Out_63_48(R3), .Out_47_32(R2), .Out_31_16(R1), .Out_15_0(R0), .CLK(CLK), .In_63_48(Write_63_48),
    .In_47_32(Write_47_32), .In_31_16(Write_31_16), .In_15_0(Write_15_0), .Write_En(en17), .Bus_En(_17),
    .Bus_En2(_49), .Out2_63_48(R7), .Out2_47_32(R6), .Out2_31_16(R5), .Out2_15_0(R4));
  Register register_19 (
    .Out_63_48(R3), .Out_47_32(R2), .Out_31_16(R1), .Out_15_0(R0), .CLK(CLK), .In_63_48(Write_63_48),
    .In_47_32(Write_47_32), .In_31_16(Write_31_16), .In_15_0(Write_15_0), .Write_En(en18), .Bus_En(_18),
    .Bus_En2(_50), .Out2_63_48(R7), .Out2_47_32(R6), .Out2_31_16(R5), .Out2_15_0(R4));
  Register register_20 (
    .Out_63_48(R3), .Out_47_32(R2), .Out_31_16(R1), .Out_15_0(R0), .CLK(CLK), .In_63_48(Write_63_48),
    .In_47_32(Write_47_32), .In_31_16(Write_31_16), .In_15_0(Write_15_0), .Write_En(en19), .Bus_En(_19),
    .Bus_En2(_51), .Out2_63_48(R7), .Out2_47_32(R6), .Out2_31_16(R5), .Out2_15_0(R4));
  Register register_21 (
    .Out_63_48(R3), .Out_47_32(R2), .Out_31_16(R1), .Out_15_0(R0), .CLK(CLK), .In_63_48(Write_63_48),
    .In_47_32(Write_47_32), .In_31_16(Write_31_16), .In_15_0(Write_15_0), .Write_En(en20), .Bus_En(_20),
    .Bus_En2(_52), .Out2_63_48(R7), .Out2_47_32(R6), .Out2_31_16(R5), .Out2_15_0(R4));
  Register register_22 (
    .Out_63_48(R3), .Out_47_32(R2), .Out_31_16(R1), .Out_15_0(R0), .CLK(CLK), .In_63_48(Write_63_48),
    .In_47_32(Write_47_32), .In_31_16(Write_31_16), .In_15_0(Write_15_0), .Write_En(en21), .Bus_En(_21),
    .Bus_En2(_53), .Out2_63_48(R7), .Out2_47_32(R6), .Out2_31_16(R5), .Out2_15_0(R4));
  Register register_23 (
    .Out_63_48(R3), .Out_47_32(R2), .Out_31_16(R1), .Out_15_0(R0), .CLK(CLK), .In_63_48(Write_63_48),
    .In_47_32(Write_47_32), .In_31_16(Write_31_16), .In_15_0(Write_15_0), .Write_En(en22), .Bus_En(_22),
    .Bus_En2(_54), .Out2_63_48(R7), .Out2_47_32(R6), .Out2_31_16(R5), .Out2_15_0(R4));
  Register register_24 (
    .Out_63_48(R3), .Out_47_32(R2), .Out_31_16(R1), .Out_15_0(R0), .CLK(CLK), .In_63_48(Write_63_48),
    .In_47_32(Write_47_32), .In_31_16(Write_31_16), .In_15_0(Write_15_0), .Write_En(en23), .Bus_En(_23),
    .Bus_En2(_55), .Out2_63_48(R7), .Out2_47_32(R6), .Out2_31_16(R5), .Out2_15_0(R4));
  Register register_25 (
    .Out_63_48(R3), .Out_47_32(R2), .Out_31_16(R1), .Out_15_0(R0), .CLK(CLK), .In_63_48(Write_63_48),
    .In_47_32(Write_47_32), .In_31_16(Write_31_16), .In_15_0(Write_15_0), .Write_En(en24), .Bus_En(_24),
    .Bus_En2(_56), .Out2_63_48(R7), .Out2_47_32(R6), .Out2_31_16(R5), .Out2_15_0(R4));
  Register register_26 (
    .Out_63_48(R3), .Out_47_32(R2), .Out_31_16(R1), .Out_15_0(R0), .CLK(CLK), .In_63_48(Write_63_48),
    .In_47_32(Write_47_32), .In_31_16(Write_31_16), .In_15_0(Write_15_0), .Write_En(en25), .Bus_En(_25),
    .Bus_En2(_57), .Out2_63_48(R7), .Out2_47_32(R6), .Out2_31_16(R5), .Out2_15_0(R4));
  Register register_27 (
    .Out_63_48(R3), .Out_47_32(R2), .Out_31_16(R1), .Out_15_0(R0), .CLK(CLK), .In_63_48(Write_63_48),
    .In_47_32(Write_47_32), .In_31_16(Write_31_16), .In_15_0(Write_15_0), .Write_En(en26), .Bus_En(_26),
    .Bus_En2(_58), .Out2_63_48(R7), .Out2_47_32(R6), .Out2_31_16(R5), .Out2_15_0(R4));
  Register register_28 (
    .Out_63_48(R3), .Out_47_32(R2), .Out_31_16(R1), .Out_15_0(R0), .CLK(CLK), .In_63_48(Write_63_48),
    .In_47_32(Write_47_32), .In_31_16(Write_31_16), .In_15_0(Write_15_0), .Write_En(en27), .Bus_En(_27),
    .Bus_En2(_59), .Out2_63_48(R7), .Out2_47_32(R6), .Out2_31_16(R5), .Out2_15_0(R4));
  Register register_29 (
    .Out_63_48(R3), .Out_47_32(R2), .Out_31_16(R1), .Out_15_0(R0), .CLK(CLK), .In_63_48(Write_63_48),
    .In_47_32(Write_47_32), .In_31_16(Write_31_16), .In_15_0(Write_15_0), .Write_En(en28), .Bus_En(_28),
    .Bus_En2(_60), .Out2_63_48(R7), .Out2_47_32(R6), .Out2_31_16(R5), .Out2_15_0(R4));
  Register register_30 (
    .Out_63_48(R3), .Out_47_32(R2), .Out_31_16(R1), .Out_15_0(R0), .CLK(CLK), .In_63_48(Write_63_48),
    .In_47_32(Write_47_32), .In_31_16(Write_31_16), .In_15_0(Write_15_0), .Write_En(en29), .Bus_En(_29),
    .Bus_En2(_61), .Out2_63_48(R7), .Out2_47_32(R6), .Out2_31_16(R5), .Out2_15_0(R4));
  Register register_31 (
    .Out_63_48(R3), .Out_47_32(R2), .Out_31_16(R1), .Out_15_0(R0), .CLK(CLK), .In_63_48(Write_63_48),
    .In_47_32(Write_47_32), .In_31_16(Write_31_16), .In_15_0(Write_15_0), .Write_En(en30), .Bus_En(_30),
    .Bus_En2(_62), .Out2_63_48(R7), .Out2_47_32(R6), .Out2_31_16(R5), .Out2_15_0(R4));
  Register register_32 (
    .Out_63_48(R3), .Out_47_32(R2), .Out_31_16(R1), .Out_15_0(R0), .CLK(CLK), .In_63_48(Write_63_48),
    .In_47_32(Write_47_32), .In_31_16(Write_31_16), .In_15_0(Write_15_0), .Write_En(en31), .Bus_En(_31),
    .Bus_En2(_63), .Out2_63_48(R7), .Out2_47_32(R6), .Out2_31_16(R5), .Out2_15_0(R4));
  _64bExtender u_64bextender_1 (
    .Current_reg(vrs), .Num16(num16), .In3(R7), .In2(R6), .In1(R5), .In0(R4), .Out3(Read2_63_48),
    .Out2(Read2_47_32), .Out1(Read2_31_16), .Out0(Read2_15_0));
  _64bExtender u_64bextender_2 (
    .Current_reg(vrd), .Num16(num16), .In3(R3), .In2(R2), .In1(R1), .In0(R0), .Out3(Read1_63_48),
    .Out2(Read1_47_32), .Out1(Read1_31_16), .Out0(Read1_15_0));

  // Other names for the same wires on the sheet: config = Reconfig; en = Write_EN; len[4:0] = length;
  //   W0[15:0] = Write_15_0; W1[15:0] = Write_31_16; W2[15:0] = Write_47_32; W3[15:0] = Write_63_48

  // Notes on the sheet:
  //   INPUTS
  //   REGISTERS
  //   VRS
  //   VRD
  //   OUTPUTS
endmodule

module Register (
  input  [15:0] In_63_48,
  input  [15:0] In_47_32,
  input  [15:0] In_31_16,
  input  [15:0] In_15_0,
  input  CLK,
  input  Write_En,
  input  Bus_En,
  input  Bus_En2,
  output [15:0] Out_63_48,
  output [15:0] Out2_63_48,
  output [15:0] Out_47_32,
  output [15:0] Out2_47_32,
  output [15:0] Out_31_16,
  output [15:0] Out2_31_16,
  output [15:0] Out_15_0,
  output [15:0] Out2_15_0
);

  wire [15:0] register_1_q, register_2_q, register_3_q, register_4_q;

  Register_part #(.width(16)) register_1 (.D(In_63_48), .en(Write_En), .Q(register_1_q), .clk(CLK));  // open: clr
  Register_part #(.width(16)) register_2 (.D(In_47_32), .en(Write_En), .Q(register_2_q), .clk(CLK));  // open: clr
  Register_part #(.width(16)) register_3 (.D(In_31_16), .en(Write_En), .Q(register_3_q), .clk(CLK));  // open: clr
  Register_part #(.width(16)) register_4 (.D(In_15_0), .en(Write_En), .Q(register_4_q), .clk(CLK));  // open: clr
  assign Out_63_48 = Bus_En ? register_1_q : 16'bz;  // Controlled_Buffer controlled_buffer_1
  assign Out_47_32 = Bus_En ? register_2_q : 16'bz;  // Controlled_Buffer controlled_buffer_2
  assign Out_31_16 = Bus_En ? register_3_q : 16'bz;  // Controlled_Buffer controlled_buffer_3
  assign Out_15_0 = Bus_En ? register_4_q : 16'bz;  // Controlled_Buffer controlled_buffer_4
  assign Out2_63_48 = Bus_En2 ? register_1_q : 16'bz;  // Controlled_Buffer controlled_buffer_5
  assign Out2_47_32 = Bus_En2 ? register_2_q : 16'bz;  // Controlled_Buffer controlled_buffer_6
  assign Out2_31_16 = Bus_En2 ? register_3_q : 16'bz;  // Controlled_Buffer controlled_buffer_7
  assign Out2_15_0 = Bus_En2 ? register_4_q : 16'bz;  // Controlled_Buffer controlled_buffer_8

  // Other names for the same wires on the sheet: En = Bus_En; En2 = Bus_En2
endmodule

module _64bALU (
  input  [15:0] A0,
  input  [15:0] A1,
  input  [15:0] A2,
  input  [15:0] A3,
  input  [15:0] B0,
  input  [15:0] B1,
  input  [15:0] B2,
  input  [15:0] B3,
  input  [2:0] ALU_Op,
  output [15:0] Q0,
  output [15:0] Q1,
  output [15:0] Q2,
  output [15:0] Q3
);

  _16bALU u_16balu_1 (.A(A0), .B(B0), .ALU_op(ALU_Op), .Result(Q0));
  _16bALU u_16balu_2 (.A(A1), .B(B1), .ALU_op(ALU_Op), .Result(Q1));
  _16bALU u_16balu_3 (.A(A2), .B(B2), .ALU_op(ALU_Op), .Result(Q2));
  _16bALU u_16balu_4 (.A(A3), .B(B3), .ALU_op(ALU_Op), .Result(Q3));
endmodule

module _16bALU (
  input  [15:0] A,
  input  [15:0] B,
  input  [2:0] ALU_op,
  output [15:0] Result
);

  wire [15:0] add, divide, multiply, sign_ext, subtract, upper_ext, zero_ext;

  Adder #(.width(16)) adder_1 (.a(A), .b(B), .out(add));  // open: cin, cout
  Subtractor #(.width(16)) subtractor_1 (.a(A), .b(B), .out(subtract));  // open: bin, bout
  Multiplier #(.width(16)) multiplier_1 (.a(A), .b(B), .out(multiply));  // open: cin, cout
  Divider #(.width(16)) divider_1 (.a(A), .b(B), .out(divide));  // open: upper, rem
  assign upper_ext = {{8{1'b0}}, A[15:8]};  // Bit_Extender bit_extender_1
  assign sign_ext = {{8{A[7]}}, A[7:0]};  // Bit_Extender bit_extender_2
  assign zero_ext = {{8{1'b0}}, A[7:0]};  // Bit_Extender bit_extender_3
  Multiplexer #(.select(3), .width(16), .enable("false")) multiplexer_1 (
    .in0(add), .in1(subtract), .in2(multiply), .in3(divide), .in4(upper_ext), .in5(zero_ext), .in6(sign_ext),
    .in7(B), .out(Result), .sel(ALU_op));

  // Other names for the same wires on the sheet: lower[7:0] = A[7:0]; upper[7:0] = A[15:8]
endmodule

module Control (
  input  [5:0] Opcode,
  input  EX,
  output Write_En,
  output [2:0] ALU_Op,
  output Config,
  output [1:0] Reg_In,
  output sign_ext_imm,
  output load_imm,
  output is_SV,
  output alu_a_sel
);

  wire [4:0] and_1_out;
  wire [10:0] multiplexer_1_out, Vec;

  Multiplexer #(.select(4), .width(11), .enable("false")) multiplexer_1 (
    .in0(11'h10), .in1(11'h21), .in2(11'h60e), .in3(11'h1e1), .in4(11'h161), .in5(11'h41), .in6(11'h409),
    .in7(11'h40b), .in8(11'h40d), .in9(11'h40b), .in10(11'hf), .in11(11'h1), .in12(11'h3), .in13(11'h5),
    .in14(11'h7), .out(multiplexer_1_out), .sel(Opcode[3:0]));  // open: in15
  assign {alu_a_sel, is_SV, load_imm, sign_ext_imm, Reg_In, and_1_out[4], ALU_Op, and_1_out[0]} = multiplexer_1_out & Vec;  // AND_Gate and_1, 11 bits wide
  assign Vec = {{10{Opcode[5]}}, Opcode[5]};  // Bit_Extender bit_extender_1
  and and_2 (Write_En, and_1_out[0], EX);
  and and_3 (Config, and_1_out[4], EX);

  // Notes on the sheet:
  //   vcfg
  //   lv
  //   sv
  //   lvi
  //   lviu
  //   lvr
  //   vw2bh
  //   vw2bl
  //   vb2ws
  //   vb2wz
  //   vmov
  //   vadd
  //   vsub
  //   vmul
  //   vdiv
endmodule

module _16bExtender (
  input  [15:0] Value,
  input  sign_ext,
  output [15:0] Out
);

  wire [15:0] bit_extender_1_out;

  assign bit_extender_1_out = {{8{Value[7]}}, Value[7:0]};  // Bit_Extender bit_extender_1
  Multiplexer #(.width(16), .enable("false")) multiplexer_1 (
    .in0(Value), .in1(bit_extender_1_out), .out(Out), .sel(sign_ext));
endmodule

module _64bExtender (
  input  [4:0] Current_reg,
  input  [4:0] Num16,
  input  [15:0] In3,
  input  [15:0] In2,
  input  [15:0] In1,
  input  [15:0] In0,
  output [15:0] Out3,
  output [15:0] Out2,
  output [15:0] Out1,
  output [15:0] Out0
);

  wire comparator_1_gt;
  wire [5:0] adder_1_out, bit_extender_1_out, bit_extender_2_out;

  assign bit_extender_1_out = {{1{1'b0}}, Current_reg};  // Bit_Extender bit_extender_1
  assign bit_extender_2_out = {{1{1'b0}}, Num16};  // Bit_Extender bit_extender_2
  // Probe on comparator_1_gt
  Adder #(.width(6)) adder_1 (.a(bit_extender_1_out), .b(6'b000001), .out(adder_1_out));  // open: cin, cout
  _16bExtender u_16bextender_1 (.Value(In3), .sign_ext(comparator_1_gt), .Out(Out3));
  _16bExtender u_16bextender_2 (.Value(In2), .sign_ext(comparator_1_gt), .Out(Out2));
  _16bExtender u_16bextender_3 (.Value(In1), .sign_ext(comparator_1_gt), .Out(Out1));
  _16bExtender u_16bextender_4 (.Value(In0), .sign_ext(comparator_1_gt), .Out(Out0));
  Comparator #(.width(6), .mode("unsigned")) comparator_1 (
    .a(adder_1_out), .b(bit_extender_2_out), .gt(comparator_1_gt));  // open: eq, lt

  // Notes on the sheet:
  //   sign ext if reg+1 > num 16 regs
endmodule

module is8bits (
  input  [4:0] Current_reg,
  input  [4:0] Num16,
  output out_3
);

  wire [5:0] adder_1_out, bit_extender_1_out, bit_extender_2_out;

  assign bit_extender_1_out = {{1{1'b0}}, Current_reg};  // Bit_Extender bit_extender_1
  assign bit_extender_2_out = {{1{1'b0}}, Num16};  // Bit_Extender bit_extender_2
  Adder #(.width(6)) adder_1 (.a(bit_extender_1_out), .b(6'b000001), .out(adder_1_out));  // open: cin, cout
  Comparator #(.width(6), .mode("unsigned")) comparator_1 (
    .a(adder_1_out), .b(bit_extender_2_out), .gt(out_3));  // open: eq, lt

  // Notes on the sheet:
  //   sign ext if reg+1 > num 16 regs
endmodule

module LV_RAM_Decoder (
  input  [4:0] vrd,
  input  [4:0] num16,
  input  [4:0] length,
  input  [31:0] RAMOutHi,
  input  [31:0] RAMOutLo,
  output [15:0] Read1_63_48,
  output [15:0] Read1_47_32,
  output [15:0] Read1_31_16,
  output [15:0] Read1_15_0
);

  wire is8bits_1_out_3;
  wire [1:1] not_1_out;
  wire [15:0] hi_ext0, hi_ext1, hi_ext2, hi_ext3;

  is8bits is8bits_1 (.Current_reg(vrd), .Num16(num16), .out_3(is8bits_1_out_3));
  not not_1 (not_1_out[1], is8bits_1_out_3);
  assign hi_ext0 = {{8{RAMOutHi[7]}}, RAMOutHi[7:0]};  // Bit_Extender bit_extender_1
  assign hi_ext1 = {{8{RAMOutHi[15]}}, RAMOutHi[15:8]};  // Bit_Extender bit_extender_2
  assign hi_ext2 = {{8{RAMOutHi[23]}}, RAMOutHi[23:16]};  // Bit_Extender bit_extender_3
  assign hi_ext3 = {{8{RAMOutHi[31]}}, RAMOutHi[31:24]};  // Bit_Extender bit_extender_4
  Multiplexer #(.select(2), .width(16), .enable("false")) multiplexer_1 (
    .in0({16{1'b0}}), .in1(hi_ext3), .in2({16{1'b0}}), .in3(RAMOutHi[31:16]), .out(Read1_63_48),
    .sel({not_1_out[1], length[2]}));
  Multiplexer #(.select(2), .width(16), .enable("false")) multiplexer_2 (
    .in0({16{1'b0}}), .in1(hi_ext2), .in2({16{1'b0}}), .in3(RAMOutHi[15:0]), .out(Read1_47_32),
    .sel({not_1_out[1], length[2]}));
  Multiplexer #(.select(2), .width(16), .enable("false")) multiplexer_3 (
    .in0(hi_ext3), .in1(hi_ext1), .in2(RAMOutHi[31:16]), .in3(RAMOutLo[31:16]), .out(Read1_31_16),
    .sel({not_1_out[1], length[2]}));
  Multiplexer #(.select(2), .width(16), .enable("false")) multiplexer_4 (
    .in0(hi_ext2), .in1(hi_ext0), .in2(RAMOutHi[15:0]), .in3(RAMOutLo[15:0]), .out(Read1_15_0),
    .sel({not_1_out[1], length[2]}));

  // Other names for the same wires on the sheet: hi0[15:0] = RAMOutHi[15:0]; hi1[15:0] = RAMOutHi[31:16];
  //   lo0[15:0] = RAMOutLo[15:0]; lo1[15:0] = RAMOutLo[31:16]
endmodule

module SV_Reg (
  input  [4:0] vrd,
  input  [4:0] num16,
  input  [4:0] length,
  input  EX,
  input  isSV,
  input  [15:0] in3,
  input  [15:0] in2,
  input  [15:0] in1,
  input  [15:0] in0,
  output VBus32,
  output VBus64,
  output [31:0] VRegOutHi,
  output [31:0] VRegOutLo
);

  wire is8bits_1_out_3, multiplexer_3_out, multiplexer_4_out;
  wire [1:1] not_1_out;

  is8bits is8bits_1 (.Current_reg(vrd), .Num16(num16), .out_3(is8bits_1_out_3));
  not not_1 (not_1_out[1], is8bits_1_out_3);
  Multiplexer #(.select(2), .width(32), .enable("false")) multiplexer_1 (
    .in0({in1[7:0], in0[7:0], {16{1'b0}}}), .in1({in3[7:0], in2[7:0], in1[7:0], in0[7:0]}), .in2({in1, in0}),
    .in3({in3, in2}), .out(VRegOutHi), .sel({not_1_out[1], length[2]}));
  Multiplexer #(.select(2), .width(32), .enable("false")) multiplexer_2 (
    .in0({32{1'b0}}), .in1({32{1'b0}}), .in2({32{1'b0}}), .in3({in1, in0}), .out(VRegOutLo),
    .sel({not_1_out[1], length[2]}));
  Multiplexer #(.select(2), .enable("false")) multiplexer_3 (
    .in0(1'b0), .in1(1'b1), .in2(1'b1), .in3(1'b0), .out(multiplexer_3_out), .sel({not_1_out[1], length[2]}));
  Multiplexer #(.select(2), .enable("false")) multiplexer_4 (
    .in0(1'b0), .in1(1'b0), .in2(1'b0), .in3(1'b1), .out(multiplexer_4_out), .sel({not_1_out[1], length[2]}));
  and and_1 (VBus32, multiplexer_3_out, EX, isSV);
  and and_2 (VBus64, isSV, EX, multiplexer_4_out);

  // Other names for the same wires on the sheet: lo2[7:0] = in2[7:0]; v2[15:0] = in2; lo3[7:0] = in3[7:0];
  //   v3[15:0] = in3; lo0[7:0] = in0[7:0]; v0[15:0] = in0; lo1[7:0] = in1[7:0]; v1[15:0] = in1
endmodule

module ALU_A (
  input  load_imm,
  input  alu_a_sel,
  input  [15:0] reg3,
  input  [15:0] reg2,
  input  [15:0] reg1,
  input  [15:0] reg0,
  input  [4:0] vrs,
  input  [15:0] B3,
  input  sign_ext_imm,
  input  [15:0] B2,
  input  [15:0] B1,
  input  [15:0] B0,
  output [15:0] ALUa3,
  output [15:0] ALUa2,
  output [15:0] ALUa1,
  output [15:0] ALUa0
);

  wire [15:0] bit_extender_1_out, bit_extender_2_out, multiplexer_1_out, multiplexer_2_out,
       multiplexer_3_out, multiplexer_4_out, multiplexer_5_out;

  assign bit_extender_1_out = {{11{1'b0}}, vrs};  // Bit_Extender bit_extender_1
  assign bit_extender_2_out = {{11{vrs[4]}}, vrs};  // Bit_Extender bit_extender_2
  Multiplexer #(.width(16), .enable("false")) multiplexer_1 (
    .in0(bit_extender_1_out), .in1(bit_extender_2_out), .out(multiplexer_1_out), .sel(sign_ext_imm));
  Multiplexer #(.width(16), .enable("false")) multiplexer_2 (
    .in0(reg3), .in1(multiplexer_1_out), .out(multiplexer_2_out), .sel(load_imm));
  Multiplexer #(.width(16), .enable("false")) multiplexer_3 (
    .in0(reg2), .in1(multiplexer_1_out), .out(multiplexer_3_out), .sel(load_imm));
  Multiplexer #(.width(16), .enable("false")) multiplexer_4 (
    .in0(reg1), .in1(multiplexer_1_out), .out(multiplexer_4_out), .sel(load_imm));
  Multiplexer #(.width(16), .enable("false")) multiplexer_5 (
    .in0(reg0), .in1(multiplexer_1_out), .out(multiplexer_5_out), .sel(load_imm));
  Multiplexer #(.width(16), .enable("false")) multiplexer_6 (
    .in0(multiplexer_2_out), .in1(B3), .out(ALUa3), .sel(alu_a_sel));
  Multiplexer #(.width(16), .enable("false")) multiplexer_7 (
    .in0(multiplexer_3_out), .in1(B2), .out(ALUa2), .sel(alu_a_sel));
  Multiplexer #(.width(16), .enable("false")) multiplexer_8 (
    .in0(multiplexer_4_out), .in1(B1), .out(ALUa1), .sel(alu_a_sel));
  Multiplexer #(.width(16), .enable("false")) multiplexer_9 (
    .in0(multiplexer_5_out), .in1(B0), .out(ALUa0), .sel(alu_a_sel));
endmodule
